// Logisim project 23120023_LED.circ as structural Verilog: 1 circuit, main circuit main
module main (
  input  I0,
  input  I1,
  input  I2,
  input  I3
);

  wire and_1_out, and_2_out, and_3_out, and_4_out, and_5_out, and_6_out, and_7_out, and_8_out, and_9_out,
       and_10_out, and_11_out, and_12_out, and_13_out, and_14_out, and_15_out, and_16_out, D0_out, D1_out,
       D2_out, D3_out, D4_out, D5_out, D6_out, not_1_out, not_2_out, not_3_out;

  not not_1 (not_1_out, I0);
  not not_2 (not_2_out, I1);
  not not_3 (not_3_out, I2);
  and and_1 (and_1_out, I2, I0);
  and and_2 (and_2_out, not_1_out, not_3_out);
  and and_3 (and_3_out, not_1_out, not_2_out);
  and and_4 (and_4_out, not_2_out, I2);
  and and_5 (and_5_out, not_1_out, I2);
  and and_6 (and_6_out, not_1_out, not_2_out);
  and and_7 (and_7_out, I0, I1);
  and and_8 (and_8_out, I1, not_3_out);
  and and_9 (and_9_out, not_1_out, I1);
  and and_10 (and_10_out, not_2_out, I2);
  and and_11 (and_11_out, not_1_out, not_3_out);
  and and_12 (and_12_out, not_1_out, I1);
  and and_13 (and_13_out, not_1_out, not_3_out);
  and and_14 (and_14_out, I1, not_3_out);
  and and_15 (and_15_out, not_1_out, I1);
  and and_16 (and_16_out, I0, not_2_out, I2);
  or D6 (D6_out, and_1_out, and_2_out, I1, I3);
  or D5 (D5_out, and_3_out, and_4_out, and_5_out, I3);
  or D4 (D4_out, and_6_out, and_7_out, not_3_out);
  or D3 (D3_out, and_8_out, and_9_out, and_10_out, I3);
  or D2 (D2_out, and_11_out, and_12_out);
  or D1 (D1_out, I0, not_2_out, I2);
  or D0 (D0_out, and_13_out, and_14_out, and_15_out, and_16_out, I3);
  _7_Segment_Display u_7_segment_display_1 (
    .g(D3_out), .f(D5_out), .a(D6_out), .b(D4_out), .e(D2_out), .d(D0_out), .c(D1_out));  // open: dp
endmodule
